# Fritzing sketch mySafeUV_Breadboard (saved by Fritzing 0.9.3b)
circuit board: 8.46667cm x 5.64444cm
breadboards: 1

parts:
  VEML6070_UV_Index_Sensor = VEML6070 [part_number=VEML6070]
  Raspberry_Pi_3 = Raspberry Pi 3 [part_number=RPI-3-V1.2]

nets:
  VDD: VEML6070_UV_Index_Sensor.VDD, Raspberry_Pi_3.5V
  GND: VEML6070_UV_Index_Sensor.GND, Raspberry_Pi_3.GND
  N1: VEML6070_UV_Index_Sensor.SCL, Raspberry_Pi_3.GPIO3
  N2: VEML6070_UV_Index_Sensor.SDA, Raspberry_Pi_3.GPIO2

notes:
  VEML6070
  VIN: 3.3V
  (Data sheet range: 3 - 5V)

custom parts:
  VEML6070: This little sensor is a great way to add UV light sensing to any microcontroller project. The VEML6070 from Vishay has a true UV A light sensor and an I2C-controlled ADC that will take readings and integrate them for you over ~60ms to 500ms.
